# Fritzing sketch CMPE_181_Project_Schematic 2 (saved by Fritzing 0.9.3b)

parts:
  Raspberry_Pi_3 = Raspberry Pi 3 [part_number=RPI-3-V1.2]
  AM1 = AM2302 Humidity and Temperature Sensor
  Part1 = Adafruit STEMMA Soil Sensor - I2C Capacitive Moisture Sensor [part_number="Adafruit #4026"]

nets:
  3V3: Raspberry_Pi_3.3v3, Part1.VIN
  N1: Raspberry_Pi_3.GPIO2, Part1.SDA
  N2: Raspberry_Pi_3.GPIO3, Part1.SCL
  N3: Raspberry_Pi_3.GPIO4, AM1.DATA
  GND: Raspberry_Pi_3.GND, AM1.GND, Part1.GND
  5V: Raspberry_Pi_3.5V, AM1.VDD

notes:
  White - SCL
  Green - SDA
  Red - VCC 3.3V
  Black - GND
  Red - VCC 5V
  Yellow - Data
  Black - GND

custom parts:
  Adafruit STEMMA Soil Sensor - I2C Capacitive Moisture Sensor: Most low cost soil sensors are resistive style, where there's two prongs and the sensor measures the conductivity between the two. These work OK at first, but eventually start to oxidize because of the exposed metal. Even if they're gold plated! The resistivity measurement goes up and up, so you constantly have to re-calibrate your code. Also, resistive measurements don't always work in loose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
